# Fritzing sketch levelConverter_RPI_MCP3008 (saved by Fritzing 0.9.2b)
stripboards: 1

parts:
  Bauteil1 = Logic Level Converter
  IC1 = MCP3008 8-channel 10-bit ADC [part_number=MCP3008]
  J1 = female pin header, 6 pins [form="♀ (female)"]
  C2 = Ceramic Capacitor [capacitance=100nF package="100 mil [THT, multilayer]"]
  J2 = female pin header, 2 pins [form="♀ (female)"]
  J3 = female pin header, 8 pins [form="♀ (female)"]
  J4 = female pin header, 8 pins [form="♀ (female)"]
  J5 = female pin header, 8 pins [form="♀ (female)"]
  Raspberry_Pi_1 = Raspberry Pi 3 [part_number=RPI-3-V1.2]

nets:
  N1: Bauteil1.TX2_LV, J1.pin6, Raspberry_Pi_1.GIPO11
  N2: Bauteil1.RX2_LV, J1.pin5, Raspberry_Pi_1.GIPO9
  GND: Bauteil1.GND, Bauteil1.HV, IC1.no_name_yet#1, IC1.no_name_yet#6, IC1.no_name_yet#7, IC1.no_name_yet#8, J1.pin4, C2.0, C2.1, J2.pin1, J2.pin2, J4.pin1, J4.pin2, J4.pin3, J4.pin4, J4.pin5, J4.pin6, J4.pin7, J4.pin8, J5.pin1, J5.pin2, J5.pin3, J5.pin4, J5.pin5, J5.pin6, J5.pin7, J5.pin8, Raspberry_Pi_1.GND
  N3: Bauteil1.LV, J1.pin3, Raspberry_Pi_1.3V3
  N4: Bauteil1.RX_LV, J1.pin2, Raspberry_Pi_1.GIPO10
  N5: Bauteil1.TX_LV, J1.pin1, Raspberry_Pi_1.GIPO8
  N6: Bauteil1.TX_HV, IC1.no_name_yet#2
  N7: Bauteil1.RX_HV, IC1.no_name_yet#3
  N8: Bauteil1.RX2_HV, IC1.no_name_yet#4
  N9: Bauteil1.TX2_HV, IC1.no_name_yet#5
  N10: IC1.no_name_yet#9, J3.pin8
  N11: IC1.no_name_yet#10, J3.pin7
  N12: IC1.no_name_yet#11, J3.pin6
  N13: IC1.no_name_yet#12, J3.pin5
  N14: IC1.no_name_yet#13, J3.pin4
  N15: IC1.no_name_yet#14, J3.pin3
  N16: IC1.no_name_yet#15, J3.pin2
  N17: IC1.no_name_yet#16, J3.pin1
